// Logisim project my_adder.circ as structural Verilog: 3 circuits, main circuit main
module main (
  input  [15:0] B,
  input  [15:0] A,
  input  sub,
  input  [3:0] TestA,
  input  [3:0] TestB,
  output [15:0] result,
  output ovf
);

  wire fourbitadder_2_adderoutput, fourbitadder_3_adderoutput, fourbitadder_4_adderoutput;

  FourBitAdder fourbitadder_1 ();  // open: S2, S1, A3, A2, A1, A0, AdderInput, sub, B3, B2, B1, B0, S3, S4, AdderOutput, OvfDe
  FourBitAdder fourbitadder_2 (
    .S2(result[1]), .S1(result[0]), .A3(A[3]), .A2(A[2]), .A1(A[1]), .A0(A[0]), .AdderInput(1'b0), .sub(sub),
    .B3(B[3]), .B2(B[2]), .B1(B[1]), .B0(B[0]), .S3(result[2]), .S4(result[3]),
    .AdderOutput(fourbitadder_2_adderoutput));  // open: OvfDe
  FourBitAdder fourbitadder_3 (
    .S2(result[5]), .S1(result[4]), .A3(A[7]), .A2(A[6]), .A1(A[5]), .A0(A[4]),
    .AdderInput(fourbitadder_2_adderoutput), .sub(sub), .B3(B[7]), .B2(B[6]), .B1(B[5]), .B0(B[4]),
    .S3(result[6]), .S4(result[7]), .AdderOutput(fourbitadder_3_adderoutput));  // open: OvfDe
  FourBitAdder fourbitadder_4 (
    .S2(result[9]), .S1(result[8]), .A3(A[11]), .A2(A[10]), .A1(A[9]), .A0(A[8]),
    .AdderInput(fourbitadder_3_adderoutput), .sub(sub), .B3(B[11]), .B2(B[10]), .B1(B[9]), .B0(B[8]),
    .S3(result[10]), .S4(result[11]), .AdderOutput(fourbitadder_4_adderoutput));  // open: OvfDe
  FourBitAdder fourbitadder_5 (
    .S2(result[13]), .S1(result[12]), .A3(A[15]), .A2(A[14]), .A1(A[13]), .A0(A[12]),
    .AdderInput(fourbitadder_4_adderoutput), .sub(sub), .B3(B[15]), .B2(B[14]), .B1(B[13]), .B0(B[12]),
    .S3(result[14]), .S4(result[15]), .OvfDe(ovf));  // open: AdderOutput
endmodule

module FourBitAdder (
  input  B0,
  input  B1,
  input  B2,
  input  B3,
  input  sub,
  input  AdderInput,
  input  A0,
  input  A1,
  input  A2,
  input  A3,
  output S1,
  output S2,
  output S3,
  output S4,
  output AdderOutput,
  output OvfDe
);

  wire fulladder_1_adder_out, fulladder_2_adder_out, fulladder_3_adder_out, or_1_out, xor_1_out, xor_2_out,
       xor_4_out, xor_5_out;

  xor xor_1 (xor_1_out, B0, sub);
  or or_1 (or_1_out, sub, AdderInput);
  xor xor_2 (xor_2_out, B1, sub);
  xor xor_3 (OvfDe, fulladder_3_adder_out, AdderOutput);
  xor xor_4 (xor_4_out, B2, sub);
  FullAdder fulladder_1 (.Adder_input(or_1_out), .A(A0), .B(xor_1_out), .Sum(S1), .Adder_out(fulladder_1_adder_out));
  FullAdder fulladder_2 (
    .Adder_input(fulladder_1_adder_out), .A(A1), .B(xor_2_out), .Sum(S2), .Adder_out(fulladder_2_adder_out));
  FullAdder fulladder_3 (
    .Adder_input(fulladder_2_adder_out), .A(A2), .B(xor_4_out), .Sum(S3), .Adder_out(fulladder_3_adder_out));
  FullAdder fulladder_4 (.Adder_input(fulladder_3_adder_out), .A(A3), .B(xor_5_out), .Sum(S4), .Adder_out(AdderOutput));
  xor xor_5 (xor_5_out, B3, sub);
endmodule

module FullAdder (
  input  Adder_input,
  input  A,
  input  B,
  output Sum,
  output Adder_out
);

  wire and_1_out, and_2_out, xor_1_out;

  xor xor_1 (xor_1_out, A, B);
  and and_1 (and_1_out, A, B);
  xor xor_2 (Sum, Adder_input, xor_1_out);
  and and_2 (and_2_out, Adder_input, xor_1_out);
  or or_1 (Adder_out, and_2_out, and_1_out);
endmodule
