// Logisim project robot.circ as structural Verilog: 1 circuit, main circuit main
module main (
  input  in_go,
  input  in_grab,
  input  override,
  output grabbing,
  output motion,
  output warning
);

  wire and_1_out, and_3_out, Clock, not_1_out, not_2_out, not_3_out, xor_1_out;

  Clock clock_1 (.out(Clock));
  not not_1 (not_1_out, override);
  xor xor_1 (xor_1_out, grabbing, in_grab);
  not not_2 (not_2_out, grabbing);
  and and_1 (and_1_out, xor_1_out, not_1_out);
  not not_3 (not_3_out, override);
  and and_2 (warning, not_2_out, motion);
  D_Flip_Flop d_ff_1 (.D(and_1_out), .clk(Clock), .Q(grabbing));  // open: Qn, preset, reset
  and and_3 (and_3_out, in_go, not_3_out);
  D_Flip_Flop d_ff_2 (.D(and_3_out), .clk(Clock), .Q(motion));  // open: Qn, preset, reset

  // Other names for the same wires on the sheet: warning_go = motion; warning_grab = grabbing
endmodule
