// Logisim project cpu.circ as structural Verilog: 10 circuits, main circuit main
module main (
  input  reset
);

  wire add_inst, addi_inst, ALUinB, and_1_out, and_inst, beq_inst, bgt_inst, BR, clk, CmpOutput, DMwe,
       IfValidInput, input_inst, j_inst, jal, jal_inst, jr_inst, jump, jump_return, lw_inst,
       memory_latch_1_oe_latched, memory_latch_1_we_latched, nclk, not_2_out, or_10_out, output_inst, Rdst,
       Rwd, Rwe, sll_inst, srl_inst, sub_inst, sw_inst, xor_inst;
  wire [2:0] multiplexer_1_out, multiplexer_2_out, optype, Rd, Rs, Rt, shamt;
  wire [3:0] opcode;
  wire [5:0] Imm;
  wire [6:0] keyboard_1_data;
  wire [7:0] keyboard_output;
  wire [15:0] address, aluOutput, controlled_buffer_9_out, FinalOutput, ImmSX, instruction_code,
       memory_latch_1_address_latched, memory_latch_1_data_in_latched, multiplexer_3_out, multiplexer_4_out,
       multiplexer_5_out, multiplexer_6_out, multiplexer_8_out, NextPC, PCPlus1, PCPlus1andB,
       ProgramCounter_result, R1Data, R2Data, ram_1_dout;

  assign optype = beq_inst ? 3'b110 : 3'bz;  // Controlled_Buffer controlled_buffer_1
  assign optype = bgt_inst ? 3'b111 : 3'bz;  // Controlled_Buffer controlled_buffer_2
  Clock clock_1 (.out(clk));
  assign optype = add_inst ? 3'b000 : 3'bz;  // Controlled_Buffer controlled_buffer_3
  assign optype = sub_inst ? 3'b001 : 3'bz;  // Controlled_Buffer controlled_buffer_4
  assign optype = sll_inst ? 3'b010 : 3'bz;  // Controlled_Buffer controlled_buffer_5
  assign optype = srl_inst ? 3'b011 : 3'bz;  // Controlled_Buffer controlled_buffer_6
  assign optype = and_inst ? 3'b100 : 3'bz;  // Controlled_Buffer controlled_buffer_7
  assign optype = xor_inst ? 3'b101 : 3'bz;  // Controlled_Buffer controlled_buffer_8
  not not_1 (nclk, clk);
  ROM #(.addrWidth(16), .dataWidth(16)) rom_1 (.addr(ProgramCounter_result), .data(instruction_code));
  Register_HW ProgramCounter (.CLK(nclk), .Reset(reset), .WE(1'b1), .InputA(NextPC), .Result(ProgramCounter_result));
  // Probe on ProgramCounter_result
  Decoder_HW decoder_hw_1 (
    .Instrucution_code(instruction_code), .Opcode(opcode), .Rs(Rs), .Rt(Rt), .Rd(Rd), .Shamt(shamt),
    .Immediate(Imm), .Address(address));
  // Probe on opcode
  Decoder #(.select(4)) decoder_1 (
    .out0(output_inst), .out1(input_inst), .out2(jal_inst), .out3(jr_inst), .out4(j_inst), .out5(bgt_inst),
    .out6(beq_inst), .out7(sw_inst), .out8(lw_inst), .out9(xor_inst), .out10(and_inst), .out11(srl_inst),
    .out12(sll_inst), .out13(sub_inst), .out14(addi_inst), .out15(add_inst), .sel(opcode));  // open: en
  // Probe on Rs
  // Probe on PCPlus1
  ALU PCPlusOne (
    .InputA(16'h1), .aluOutput(PCPlus1), .InputB(ProgramCounter_result), .OpType(3'b000));  // open: CmpOutput
  // Probe on Rt
  // Probe on PCPlus1
  // Probe on Rd
  Multiplexer #(.width(3), .enable("false")) multiplexer_1 (.in0(Rt), .in1(Rd), .out(multiplexer_1_out), .sel(Rdst));
  Multiplexer #(.width(3), .enable("false")) multiplexer_2 (
    .in0(multiplexer_1_out), .in1(3'b111), .out(multiplexer_2_out), .sel(jal));
  // Probe on shamt
  // Probe on multiplexer_2_out
  // Probe on Imm
  // Probe on Imm
  ALU u_PCPlus1andB (.InputA(PCPlus1), .aluOutput(PCPlus1andB), .InputB(ImmSX), .OpType(3'b000));  // open: CmpOutput
  Multiplexer #(.width(16), .enable("false")) multiplexer_3 (
    .in0(FinalOutput), .in1(PCPlus1), .out(multiplexer_3_out), .sel(jal));
  Multiplexer #(.width(16), .enable("false")) multiplexer_4 (
    .in0(multiplexer_3_out), .in1({{8{1'b0}}, keyboard_output}), .out(multiplexer_4_out), .sel(input_inst));
  // Probe on address
  // Probe on multiplexer_4_out
  SignExtension signextension_1 (.InputA(Imm), .Result(ImmSX));
  // Probe on ImmSX
  not not_2 (not_2_out, CmpOutput);
  // Probe on not_2_out
  RegisterFile registerfile_1 (
    .RS2(Rt), .reset(reset), .RDVAL(multiplexer_4_out), .RD(multiplexer_2_out), .clk(clk), .RS1(Rs),
    .RegWE(Rwe), .RS1VAL(R1Data), .RS2VAL(R2Data));
  or or_1 (BR, beq_inst, bgt_inst);
  buf or_2 (jump, j_inst);  // OR_Gate
  buf or_3 (DMwe, sw_inst);  // OR_Gate
  or or_4 (Rwe, sll_inst, jal_inst, srl_inst, add_inst, addi_inst, lw_inst, sub_inst, xor_inst, and_inst, input_inst);
  or or_5 (Rdst, sll_inst, sub_inst, add_inst, xor_inst, srl_inst, and_inst);
  buf or_6 (Rwd, lw_inst);  // OR_Gate
  buf or_7 (jal, jal_inst);  // OR_Gate
  buf or_8 (jump_return, jr_inst);  // OR_Gate
  // Probe on PCPlus1
  Multiplexer #(.width(16), .enable("false")) multiplexer_5 (
    .in0(PCPlus1), .in1(PCPlus1andB), .out(multiplexer_5_out), .sel(and_1_out));
  and and_1 (and_1_out, BR, not_2_out);
  or or_9 (ALUinB, srl_inst, addi_inst, lw_inst, sll_inst, sw_inst);
  // Probe on multiplexer_5_out
  Multiplexer #(.width(16), .enable("false")) multiplexer_6 (
    .in0(multiplexer_5_out), .in1(address), .out(multiplexer_6_out), .sel(or_10_out));
  or or_10 (or_10_out, jump, jal);
  Multiplexer #(.width(16), .enable("false")) multiplexer_7 (
    .in0(multiplexer_6_out), .in1(R1Data), .out(NextPC), .sel(jump_return));
  Keyboard keyboard_1 (.clk(nclk), .re(input_inst), .clr(reset), .avail(IfValidInput), .data(keyboard_1_data));
  assign controlled_buffer_9_out = output_inst ? R1Data : 16'bz;  // Controlled_Buffer controlled_buffer_9
  Multiplexer #(.width(16), .enable("false")) multiplexer_8 (
    .in0(R2Data), .in1(ImmSX), .out(multiplexer_8_out), .sel(ALUinB));
  // Probe on ImmSX
  // Probe on multiplexer_8_out
  // Probe on R1Data
  // Probe on optype
  TTY #(.rows(13), .cols(80)) tty_1 (.data(controlled_buffer_9_out[6:0]), .clk(clk), .we(output_inst), .clr(reset));
  ALU alu_1 (
    .CmpOutput(CmpOutput), .InputA(R1Data), .aluOutput(aluOutput), .InputB(multiplexer_8_out), .OpType(optype));
  and and_2 (keyboard_output[5], keyboard_1_data[5], IfValidInput);
  and and_3 (keyboard_output[6], keyboard_1_data[6], IfValidInput);
  and and_4 (keyboard_output[0], IfValidInput, keyboard_1_data[0]);
  and and_5 (keyboard_output[1], keyboard_1_data[1], IfValidInput);
  and and_6 (keyboard_output[2], keyboard_1_data[2], IfValidInput);
  and and_7 (keyboard_output[3], keyboard_1_data[3], IfValidInput);
  and and_8 (keyboard_output[4], keyboard_1_data[4], IfValidInput);
  not not_3 (keyboard_output[7], IfValidInput);
  memory_latch memory_latch_1 (
    .address(aluOutput), .WE(DMwe), .clk(nclk), .data_in(R2Data),
    .address_latched(memory_latch_1_address_latched), .WE_latched(memory_latch_1_we_latched),
    .OE_latched(memory_latch_1_oe_latched), .data_in_latched(memory_latch_1_data_in_latched));
  RAM #(.addrWidth(16), .dataWidth(16), .trigger("high"), .databus("bibus")) ram_1 (
    .addr(memory_latch_1_address_latched), .we(memory_latch_1_we_latched), .oe(memory_latch_1_oe_latched),
    .din(memory_latch_1_data_in_latched), .dout(ram_1_dout));
  Multiplexer #(.width(16), .enable("false")) multiplexer_9 (
    .in0(aluOutput), .in1(ram_1_dout), .out(FinalOutput), .sel(Rwd));

  // Notes on the sheet:
  //   contents of rom_1 (hex, n*v repeats v):
  //   e050 e09f f458 e070 e090 d458 603f
endmodule

module memory_latch (
  input  [15:0] address,
  input  WE,
  input  clk,
  input  [15:0] data_in,
  output [15:0] address_latched,
  output WE_latched,
  output OE_latched,
  output [15:0] data_in_latched
);

  wire DMwe_latch_q;
  wire [15:0] addr_latch_q;

  Register #(.width(16), .trigger("falling")) addr_latch (
    .D(address), .en(WE), .clk(clk), .Q(addr_latch_q));  // open: clr
  D_Flip_Flop #(.trigger("falling")) DMwe_latch (.D(WE), .clk(clk), .Q(DMwe_latch_q));  // open: Qn, preset, reset
  Register #(.width(16), .trigger("falling")) data_to_be_written (
    .D(data_in), .en(WE), .clk(clk), .Q(data_in_latched));  // open: clr
  Multiplexer #(.width(16), .enable("false")) multiplexer_1 (
    .in0(address), .in1(addr_latch_q), .out(address_latched), .sel(DMwe_latch_q));
  and and_1 (WE_latched, clk, DMwe_latch_q);
  not not_1 (OE_latched, WE_latched);
endmodule

module OneBitAdder (
  input  Cin,
  input  a,
  input  b,
  output Sum,
  output Cout
);

  wire and_1_out, and_2_out, xor_1_out;

  and and_1 (and_1_out, b, a);
  xor xor_1 (xor_1_out, a, b);
  or or_1 (Cout, and_1_out, and_2_out);
  and and_2 (and_2_out, xor_1_out, Cin);
  xor xor_2 (Sum, Cin, xor_1_out);
endmodule

module SixteenAdder (
  input  AddSub,
  input  [15:0] InputA,
  input  [15:0] InputB,
  output [15:0] Sum
);

  wire onebitadder_1_cout, onebitadder_2_cout, onebitadder_3_cout, onebitadder_4_cout, onebitadder_5_cout,
       onebitadder_6_cout, onebitadder_7_cout, onebitadder_8_cout, onebitadder_9_cout, onebitadder_10_cout,
       onebitadder_11_cout, onebitadder_12_cout, onebitadder_13_cout, onebitadder_14_cout,
       onebitadder_15_cout, xor_1_out, xor_2_out, xor_3_out, xor_4_out, xor_5_out, xor_6_out, xor_7_out,
       xor_8_out, xor_9_out, xor_10_out, xor_11_out, xor_12_out, xor_13_out, xor_14_out, xor_15_out,
       xor_16_out;

  xor xor_1 (xor_1_out, AddSub, InputB[0]);
  xor xor_2 (xor_2_out, AddSub, InputB[1]);
  xor xor_3 (xor_3_out, AddSub, InputB[2]);
  xor xor_4 (xor_4_out, AddSub, InputB[3]);
  xor xor_5 (xor_5_out, AddSub, InputB[4]);
  xor xor_6 (xor_6_out, AddSub, InputB[5]);
  xor xor_7 (xor_7_out, AddSub, InputB[6]);
  xor xor_8 (xor_8_out, AddSub, InputB[7]);
  xor xor_9 (xor_9_out, AddSub, InputB[8]);
  xor xor_10 (xor_10_out, AddSub, InputB[9]);
  xor xor_11 (xor_11_out, AddSub, InputB[10]);
  xor xor_12 (xor_12_out, AddSub, InputB[11]);
  xor xor_13 (xor_13_out, AddSub, InputB[12]);
  xor xor_14 (xor_14_out, AddSub, InputB[13]);
  xor xor_15 (xor_15_out, AddSub, InputB[14]);
  xor xor_16 (xor_16_out, AddSub, InputB[15]);
  OneBitAdder onebitadder_1 (.Cin(AddSub), .a(InputA[0]), .b(xor_1_out), .Sum(Sum[0]), .Cout(onebitadder_1_cout));
  OneBitAdder onebitadder_2 (
    .Cin(onebitadder_1_cout), .a(InputA[1]), .b(xor_2_out), .Sum(Sum[1]), .Cout(onebitadder_2_cout));
  OneBitAdder onebitadder_3 (
    .Cin(onebitadder_2_cout), .a(InputA[2]), .b(xor_3_out), .Sum(Sum[2]), .Cout(onebitadder_3_cout));
  OneBitAdder onebitadder_4 (
    .Cin(onebitadder_3_cout), .a(InputA[3]), .b(xor_4_out), .Sum(Sum[3]), .Cout(onebitadder_4_cout));
  OneBitAdder onebitadder_5 (
    .Cin(onebitadder_4_cout), .a(InputA[4]), .b(xor_5_out), .Sum(Sum[4]), .Cout(onebitadder_5_cout));
  OneBitAdder onebitadder_6 (
    .Cin(onebitadder_5_cout), .a(InputA[5]), .b(xor_6_out), .Sum(Sum[5]), .Cout(onebitadder_6_cout));
  OneBitAdder onebitadder_7 (
    .Cin(onebitadder_6_cout), .a(InputA[6]), .b(xor_7_out), .Sum(Sum[6]), .Cout(onebitadder_7_cout));
  OneBitAdder onebitadder_8 (
    .Cin(onebitadder_7_cout), .a(InputA[7]), .b(xor_8_out), .Sum(Sum[7]), .Cout(onebitadder_8_cout));
  OneBitAdder onebitadder_9 (
    .Cin(onebitadder_8_cout), .a(InputA[8]), .b(xor_9_out), .Sum(Sum[8]), .Cout(onebitadder_9_cout));
  OneBitAdder onebitadder_10 (
    .Cin(onebitadder_9_cout), .a(InputA[9]), .b(xor_10_out), .Sum(Sum[9]), .Cout(onebitadder_10_cout));
  OneBitAdder onebitadder_11 (
    .Cin(onebitadder_10_cout), .a(InputA[10]), .b(xor_11_out), .Sum(Sum[10]), .Cout(onebitadder_11_cout));
  OneBitAdder onebitadder_12 (
    .Cin(onebitadder_11_cout), .a(InputA[11]), .b(xor_12_out), .Sum(Sum[11]), .Cout(onebitadder_12_cout));
  OneBitAdder onebitadder_13 (
    .Cin(onebitadder_12_cout), .a(InputA[12]), .b(xor_13_out), .Sum(Sum[12]), .Cout(onebitadder_13_cout));
  OneBitAdder onebitadder_14 (
    .Cin(onebitadder_13_cout), .a(InputA[13]), .b(xor_14_out), .Sum(Sum[13]), .Cout(onebitadder_14_cout));
  OneBitAdder onebitadder_15 (
    .Cin(onebitadder_14_cout), .a(InputA[14]), .b(xor_15_out), .Sum(Sum[14]), .Cout(onebitadder_15_cout));
  OneBitAdder onebitadder_16 (.Cin(onebitadder_15_cout), .a(InputA[15]), .b(xor_16_out), .Sum(Sum[15]));  // open: Cout

  // Other names for the same wires on the sheet: A0 = InputA[0]; A1 = InputA[1]; A2 = InputA[2]; A3 = InputA[3];
  //   A4 = InputA[4]; A5 = InputA[5]; A6 = InputA[6]; A7 = InputA[7]; A8 = InputA[8]; A9 = InputA[9];
  //   A10 = InputA[10]; A11 = InputA[11]; A12 = InputA[12]; A13 = InputA[13]; A14 = InputA[14]; A15 = InputA[15];
  //   B0 = InputB[0]; B1 = InputB[1]; B2 = InputB[2]; B3 = InputB[3]; B4 = InputB[4]; B5 = InputB[5]; B6 = InputB[6];
  //   B7 = InputB[7]; B8 = InputB[8]; B9 = InputB[9]; B10 = InputB[10]; B11 = InputB[11]; B12 = InputB[12];
  //   B13 = InputB[13]; B14 = InputB[14]; B15 = InputB[15]; S0 = Sum[0]; S1 = Sum[1]; S2 = Sum[2]; S3 = Sum[3];
  //   S4 = Sum[4]; S5 = Sum[5]; S6 = Sum[6]; S7 = Sum[7]; S8 = Sum[8]; S9 = Sum[9]; S10 = Sum[10]; S11 = Sum[11];
  //   S12 = Sum[12]; S13 = Sum[13]; S14 = Sum[14]; S15 = Sum[15]
endmodule

module Shifter_HW (
  input  [2:0] Input_num,
  input  [15:0] InputA,
  output [15:0] Result
);

  wire multiplexer_1_out, multiplexer_2_out, multiplexer_3_out, multiplexer_4_out, multiplexer_5_out,
       multiplexer_6_out, multiplexer_7_out, multiplexer_8_out, multiplexer_9_out, multiplexer_10_out,
       multiplexer_11_out, multiplexer_12_out, multiplexer_13_out, multiplexer_14_out, multiplexer_15_out,
       multiplexer_16_out, multiplexer_17_out, multiplexer_18_out, multiplexer_19_out, multiplexer_20_out,
       multiplexer_21_out, multiplexer_22_out, multiplexer_23_out, multiplexer_24_out, multiplexer_25_out,
       multiplexer_26_out, multiplexer_27_out, multiplexer_28_out, multiplexer_29_out, multiplexer_30_out,
       multiplexer_31_out, multiplexer_32_out;

  Multiplexer #(.enable("false")) multiplexer_1 (
    .in0(InputA[15]), .in1(InputA[11]), .out(multiplexer_1_out), .sel(Input_num[2]));
  Multiplexer #(.enable("false")) multiplexer_2 (
    .in0(InputA[14]), .in1(InputA[10]), .out(multiplexer_2_out), .sel(Input_num[2]));
  Multiplexer #(.enable("false")) multiplexer_3 (
    .in0(InputA[13]), .in1(InputA[9]), .out(multiplexer_3_out), .sel(Input_num[2]));
  Multiplexer #(.enable("false")) multiplexer_4 (
    .in0(InputA[12]), .in1(InputA[8]), .out(multiplexer_4_out), .sel(Input_num[2]));
  Multiplexer #(.enable("false")) multiplexer_5 (
    .in0(InputA[11]), .in1(InputA[7]), .out(multiplexer_5_out), .sel(Input_num[2]));
  Multiplexer #(.enable("false")) multiplexer_6 (
    .in0(InputA[10]), .in1(InputA[6]), .out(multiplexer_6_out), .sel(Input_num[2]));
  Multiplexer #(.enable("false")) multiplexer_7 (
    .in0(InputA[9]), .in1(InputA[5]), .out(multiplexer_7_out), .sel(Input_num[2]));
  Multiplexer #(.enable("false")) multiplexer_8 (
    .in0(InputA[8]), .in1(InputA[4]), .out(multiplexer_8_out), .sel(Input_num[2]));
  Multiplexer #(.enable("false")) multiplexer_9 (
    .in0(InputA[7]), .in1(InputA[3]), .out(multiplexer_9_out), .sel(Input_num[2]));
  Multiplexer #(.enable("false")) multiplexer_10 (
    .in0(InputA[6]), .in1(InputA[2]), .out(multiplexer_10_out), .sel(Input_num[2]));
  Multiplexer #(.enable("false")) multiplexer_11 (
    .in0(InputA[5]), .in1(InputA[1]), .out(multiplexer_11_out), .sel(Input_num[2]));
  Multiplexer #(.enable("false")) multiplexer_12 (
    .in0(InputA[4]), .in1(InputA[0]), .out(multiplexer_12_out), .sel(Input_num[2]));
  Multiplexer #(.enable("false")) multiplexer_13 (
    .in0(InputA[3]), .in1(1'b0), .out(multiplexer_13_out), .sel(Input_num[2]));
  Multiplexer #(.enable("false")) multiplexer_14 (
    .in0(InputA[2]), .in1(1'b0), .out(multiplexer_14_out), .sel(Input_num[2]));
  Multiplexer #(.enable("false")) multiplexer_15 (
    .in0(InputA[1]), .in1(1'b0), .out(multiplexer_15_out), .sel(Input_num[2]));
  Multiplexer #(.enable("false")) multiplexer_16 (
    .in0(InputA[0]), .in1(1'b0), .out(multiplexer_16_out), .sel(Input_num[2]));
  Multiplexer #(.enable("false")) multiplexer_17 (
    .in0(multiplexer_1_out), .in1(multiplexer_3_out), .out(multiplexer_17_out), .sel(Input_num[1]));
  Multiplexer #(.enable("false")) multiplexer_18 (
    .in0(multiplexer_2_out), .in1(multiplexer_4_out), .out(multiplexer_18_out), .sel(Input_num[1]));
  Multiplexer #(.enable("false")) multiplexer_19 (
    .in0(multiplexer_3_out), .in1(multiplexer_5_out), .out(multiplexer_19_out), .sel(Input_num[1]));
  Multiplexer #(.enable("false")) multiplexer_20 (
    .in0(multiplexer_4_out), .in1(multiplexer_6_out), .out(multiplexer_20_out), .sel(Input_num[1]));
  Multiplexer #(.enable("false")) multiplexer_21 (
    .in0(multiplexer_5_out), .in1(multiplexer_7_out), .out(multiplexer_21_out), .sel(Input_num[1]));
  Multiplexer #(.enable("false")) multiplexer_22 (
    .in0(multiplexer_6_out), .in1(multiplexer_8_out), .out(multiplexer_22_out), .sel(Input_num[1]));
  Multiplexer #(.enable("false")) multiplexer_23 (
    .in0(multiplexer_7_out), .in1(multiplexer_9_out), .out(multiplexer_23_out), .sel(Input_num[1]));
  Multiplexer #(.enable("false")) multiplexer_24 (
    .in0(multiplexer_8_out), .in1(multiplexer_10_out), .out(multiplexer_24_out), .sel(Input_num[1]));
  Multiplexer #(.enable("false")) multiplexer_25 (
    .in0(multiplexer_9_out), .in1(multiplexer_11_out), .out(multiplexer_25_out), .sel(Input_num[1]));
  Multiplexer #(.enable("false")) multiplexer_26 (
    .in0(multiplexer_10_out), .in1(multiplexer_12_out), .out(multiplexer_26_out), .sel(Input_num[1]));
  Multiplexer #(.enable("false")) multiplexer_27 (
    .in0(multiplexer_11_out), .in1(multiplexer_13_out), .out(multiplexer_27_out), .sel(Input_num[1]));
  Multiplexer #(.enable("false")) multiplexer_28 (
    .in0(multiplexer_12_out), .in1(multiplexer_14_out), .out(multiplexer_28_out), .sel(Input_num[1]));
  Multiplexer #(.enable("false")) multiplexer_29 (
    .in0(multiplexer_13_out), .in1(multiplexer_15_out), .out(multiplexer_29_out), .sel(Input_num[1]));
  Multiplexer #(.enable("false")) multiplexer_30 (
    .in0(multiplexer_14_out), .in1(multiplexer_16_out), .out(multiplexer_30_out), .sel(Input_num[1]));
  Multiplexer #(.enable("false")) multiplexer_31 (
    .in0(multiplexer_15_out), .in1(1'b0), .out(multiplexer_31_out), .sel(Input_num[1]));
  Multiplexer #(.enable("false")) multiplexer_32 (
    .in0(multiplexer_16_out), .in1(1'b0), .out(multiplexer_32_out), .sel(Input_num[1]));
  Multiplexer #(.enable("false")) multiplexer_33 (
    .in0(multiplexer_17_out), .in1(multiplexer_18_out), .out(Result[15]), .sel(Input_num[0]));
  Multiplexer #(.enable("false")) multiplexer_34 (
    .in0(multiplexer_18_out), .in1(multiplexer_19_out), .out(Result[14]), .sel(Input_num[0]));
  Multiplexer #(.enable("false")) multiplexer_35 (
    .in0(multiplexer_19_out), .in1(multiplexer_20_out), .out(Result[13]), .sel(Input_num[0]));
  Multiplexer #(.enable("false")) multiplexer_36 (
    .in0(multiplexer_20_out), .in1(multiplexer_21_out), .out(Result[12]), .sel(Input_num[0]));
  Multiplexer #(.enable("false")) multiplexer_37 (
    .in0(multiplexer_21_out), .in1(multiplexer_22_out), .out(Result[11]), .sel(Input_num[0]));
  Multiplexer #(.enable("false")) multiplexer_38 (
    .in0(multiplexer_22_out), .in1(multiplexer_23_out), .out(Result[10]), .sel(Input_num[0]));
  Multiplexer #(.enable("false")) multiplexer_39 (
    .in0(multiplexer_23_out), .in1(multiplexer_24_out), .out(Result[9]), .sel(Input_num[0]));
  Multiplexer #(.enable("false")) multiplexer_40 (
    .in0(multiplexer_24_out), .in1(multiplexer_25_out), .out(Result[8]), .sel(Input_num[0]));
  Multiplexer #(.enable("false")) multiplexer_41 (
    .in0(multiplexer_25_out), .in1(multiplexer_26_out), .out(Result[7]), .sel(Input_num[0]));
  Multiplexer #(.enable("false")) multiplexer_42 (
    .in0(multiplexer_26_out), .in1(multiplexer_27_out), .out(Result[6]), .sel(Input_num[0]));
  Multiplexer #(.enable("false")) multiplexer_43 (
    .in0(multiplexer_27_out), .in1(multiplexer_28_out), .out(Result[5]), .sel(Input_num[0]));
  Multiplexer #(.enable("false")) multiplexer_44 (
    .in0(multiplexer_28_out), .in1(multiplexer_29_out), .out(Result[4]), .sel(Input_num[0]));
  Multiplexer #(.enable("false")) multiplexer_45 (
    .in0(multiplexer_29_out), .in1(multiplexer_30_out), .out(Result[3]), .sel(Input_num[0]));
  Multiplexer #(.enable("false")) multiplexer_46 (
    .in0(multiplexer_30_out), .in1(multiplexer_31_out), .out(Result[2]), .sel(Input_num[0]));
  Multiplexer #(.enable("false")) multiplexer_47 (
    .in0(multiplexer_31_out), .in1(multiplexer_32_out), .out(Result[1]), .sel(Input_num[0]));
  Multiplexer #(.enable("false")) multiplexer_48 (
    .in0(multiplexer_32_out), .in1(1'b0), .out(Result[0]), .sel(Input_num[0]));

  // Other names for the same wires on the sheet: Shift0 = Input_num[0]; Shift1 = Input_num[1]; Shift2 = Input_num[2];
  //   A0 = InputA[0]; A1 = InputA[1]; A2 = InputA[2]; A3 = InputA[3]; A4 = InputA[4]; A5 = InputA[5]; A6 = InputA[6];
  //   A7 = InputA[7]; A8 = InputA[8]; A9 = InputA[9]; A10 = InputA[10]; A11 = InputA[11]; A12 = InputA[12];
  //   A13 = InputA[13]; A14 = InputA[14]; A15 = InputA[15]; S0 = Result[0]; S1 = Result[1]; S2 = Result[2];
  //   S3 = Result[3]; S4 = Result[4]; S5 = Result[5]; S6 = Result[6]; S7 = Result[7]; S8 = Result[8]; S9 = Result[9];
  //   S10 = Result[10]; S11 = Result[11]; S12 = Result[12]; S13 = Result[13]; S14 = Result[14]; S15 = Result[15]
endmodule

module Decoder_HW (
  input  [15:0] Instrucution_code,
  output [3:0] Opcode,
  output [2:0] Rs,
  output [2:0] Rt,
  output [2:0] Rd,
  output [2:0] Shamt,
  output [5:0] Immediate,
  output [15:0] Address
);


  assign Address = {4'b0000, Instrucution_code[11:0]};
  assign Immediate = Instrucution_code[5:0];
  assign Opcode = Instrucution_code[15:12];
  assign Rd = Instrucution_code[5:3];
  assign Rs = Instrucution_code[11:9];
  assign Rt = Instrucution_code[8:6];
  assign Shamt = Instrucution_code[2:0];

  // Other names for the same wires on the sheet: A0 = Instrucution_code[0]; Address_t[11:0] = Instrucution_code[11:0];
  //   A1 = Instrucution_code[1]; A2 = Instrucution_code[2]; A3 = Instrucution_code[3]; A4 = Instrucution_code[4];
  //   A5 = Instrucution_code[5]; A6 = Instrucution_code[6]; A7 = Instrucution_code[7]; A8 = Instrucution_code[8];
  //   A9 = Instrucution_code[9]; A10 = Instrucution_code[10]; A11 = Instrucution_code[11];
  //   A12 = Instrucution_code[12]; A13 = Instrucution_code[13]; A14 = Instrucution_code[14];
  //   A15 = Instrucution_code[15]
endmodule

module Register_HW (
  input  CLK,
  input  Reset,
  input  WE,
  input  [15:0] InputA,
  output [15:0] Result
);

  wire clk_enable;

  D_Flip_Flop d_ff_1 (.D(InputA[0]), .clk(clk_enable), .Q(Result[0]), .reset(Reset));  // open: Qn, preset
  D_Flip_Flop d_ff_2 (.D(InputA[4]), .clk(clk_enable), .Q(Result[4]), .reset(Reset));  // open: Qn, preset
  D_Flip_Flop d_ff_3 (.D(InputA[8]), .clk(clk_enable), .Q(Result[8]), .reset(Reset));  // open: Qn, preset
  D_Flip_Flop d_ff_4 (.D(InputA[12]), .clk(clk_enable), .Q(Result[12]), .reset(Reset));  // open: Qn, preset
  D_Flip_Flop d_ff_5 (.D(InputA[1]), .clk(clk_enable), .Q(Result[1]), .reset(Reset));  // open: Qn, preset
  D_Flip_Flop d_ff_6 (.D(InputA[5]), .clk(clk_enable), .Q(Result[5]), .reset(Reset));  // open: Qn, preset
  D_Flip_Flop d_ff_7 (.D(InputA[9]), .clk(clk_enable), .Q(Result[9]), .reset(Reset));  // open: Qn, preset
  D_Flip_Flop d_ff_8 (.D(InputA[13]), .clk(clk_enable), .Q(Result[13]), .reset(Reset));  // open: Qn, preset
  and and_1 (clk_enable, CLK, WE);
  D_Flip_Flop d_ff_9 (.D(InputA[2]), .clk(clk_enable), .Q(Result[2]), .reset(Reset));  // open: Qn, preset
  D_Flip_Flop d_ff_10 (.D(InputA[6]), .clk(clk_enable), .Q(Result[6]), .reset(Reset));  // open: Qn, preset
  D_Flip_Flop d_ff_11 (.D(InputA[10]), .clk(clk_enable), .Q(Result[10]), .reset(Reset));  // open: Qn, preset
  D_Flip_Flop d_ff_12 (.D(InputA[14]), .clk(clk_enable), .Q(Result[14]), .reset(Reset));  // open: Qn, preset
  D_Flip_Flop d_ff_13 (.D(InputA[3]), .clk(clk_enable), .Q(Result[3]), .reset(Reset));  // open: Qn, preset
  D_Flip_Flop d_ff_14 (.D(InputA[7]), .clk(clk_enable), .Q(Result[7]), .reset(Reset));  // open: Qn, preset
  D_Flip_Flop d_ff_15 (.D(InputA[11]), .clk(clk_enable), .Q(Result[11]), .reset(Reset));  // open: Qn, preset
  D_Flip_Flop d_ff_16 (.D(InputA[15]), .clk(clk_enable), .Q(Result[15]), .reset(Reset));  // open: Qn, preset

  // Other names for the same wires on the sheet: A0 = InputA[0]; A1 = InputA[1]; A2 = InputA[2]; A3 = InputA[3];
  //   A4 = InputA[4]; A5 = InputA[5]; A6 = InputA[6]; A7 = InputA[7]; A8 = InputA[8]; A9 = InputA[9];
  //   A10 = InputA[10]; A11 = InputA[11]; A12 = InputA[12]; A13 = InputA[13]; A14 = InputA[14]; A15 = InputA[15];
  //   S0 = Result[0]; S1 = Result[1]; S2 = Result[2]; S3 = Result[3]; S4 = Result[4]; S5 = Result[5]; S6 = Result[6];
  //   S7 = Result[7]; S8 = Result[8]; S9 = Result[9]; S10 = Result[10]; S11 = Result[11]; S12 = Result[12];
  //   S13 = Result[13]; S14 = Result[14]; S15 = Result[15]
endmodule

module RegisterFile (
  input  clk,
  input  reset,
  input  RegWE,
  input  [15:0] RDVAL,
  input  [2:0] RD,
  input  [2:0] RS1,
  input  [2:0] RS2,
  output [15:0] RS1VAL,
  output [15:0] RS2VAL
);

  wire RS1_0, RS1_1, RS1_2, RS1_3, RS1_4, RS1_5, RS1_6, RS1_7, RS2_0, RS2_1, RS2_2, RS2_3, RS2_4, RS2_5,
       RS2_6, RS2_7, WE0, WE1, WE2, WE3, WE4, WE5, WE6, WE7;
  wire [15:0] OutputR0, OutputR1, OutputR2, OutputR3, OutputR4, OutputR5, OutputR6, OutputR7;

  Decoder #(.select(3)) decoder_1 (
    .out0(WE0), .out1(WE1), .out2(WE2), .out3(WE3), .out4(WE4), .out5(WE5), .out6(WE6), .out7(WE7), .sel(RD),
    .en(RegWE));
  assign RS1VAL = RS1_7 ? OutputR7 : 16'bz;  // Controlled_Buffer controlled_buffer_1
  assign RS1VAL = RS1_6 ? OutputR6 : 16'bz;  // Controlled_Buffer controlled_buffer_2
  assign RS1VAL = RS1_5 ? OutputR5 : 16'bz;  // Controlled_Buffer controlled_buffer_3
  assign RS1VAL = RS1_4 ? OutputR4 : 16'bz;  // Controlled_Buffer controlled_buffer_4
  assign RS1VAL = RS1_3 ? OutputR3 : 16'bz;  // Controlled_Buffer controlled_buffer_5
  assign RS1VAL = RS1_2 ? OutputR2 : 16'bz;  // Controlled_Buffer controlled_buffer_6
  assign RS1VAL = RS1_1 ? OutputR1 : 16'bz;  // Controlled_Buffer controlled_buffer_7
  assign RS1VAL = RS1_0 ? OutputR0 : 16'bz;  // Controlled_Buffer controlled_buffer_8
  assign RS2VAL = RS2_7 ? OutputR7 : 16'bz;  // Controlled_Buffer controlled_buffer_9
  assign RS2VAL = RS2_6 ? OutputR6 : 16'bz;  // Controlled_Buffer controlled_buffer_10
  assign RS2VAL = RS2_5 ? OutputR5 : 16'bz;  // Controlled_Buffer controlled_buffer_11
  assign RS2VAL = RS2_4 ? OutputR4 : 16'bz;  // Controlled_Buffer controlled_buffer_12
  assign RS2VAL = RS2_3 ? OutputR3 : 16'bz;  // Controlled_Buffer controlled_buffer_13
  assign RS2VAL = RS2_2 ? OutputR2 : 16'bz;  // Controlled_Buffer controlled_buffer_14
  assign RS2VAL = RS2_1 ? OutputR1 : 16'bz;  // Controlled_Buffer controlled_buffer_15
  assign RS2VAL = RS2_0 ? OutputR0 : 16'bz;  // Controlled_Buffer controlled_buffer_16
  Register_HW Register0 (.CLK(clk), .Reset(reset), .WE(WE0), .InputA(RDVAL), .Result(OutputR0));
  Register_HW Register1 (.CLK(clk), .Reset(reset), .WE(WE1), .InputA(RDVAL), .Result(OutputR1));
  Register_HW Register3 (.CLK(clk), .Reset(reset), .WE(WE3), .InputA(RDVAL), .Result(OutputR3));
  Register_HW Register5 (.CLK(clk), .Reset(reset), .WE(WE5), .InputA(RDVAL), .Result(OutputR5));
  Register_HW Register7 (.CLK(clk), .Reset(reset), .WE(WE7), .InputA(RDVAL), .Result(OutputR7));
  Decoder #(.select(3)) decoder_2 (
    .out0(RS1_0), .out1(RS1_1), .out2(RS1_2), .out3(RS1_3), .out4(RS1_4), .out5(RS1_5), .out6(RS1_6),
    .out7(RS1_7), .sel(RS1));  // open: en
  // Probe on OutputR0
  // Probe on OutputR1
  // Probe on OutputR3
  // Probe on OutputR5
  // Probe on OutputR7
  Decoder #(.select(3)) decoder_3 (
    .out0(RS2_0), .out1(RS2_1), .out2(RS2_2), .out3(RS2_3), .out4(RS2_4), .out5(RS2_5), .out6(RS2_6),
    .out7(RS2_7), .sel(RS2));  // open: en
  Register_HW Register2 (.CLK(clk), .Reset(reset), .WE(WE2), .InputA(RDVAL), .Result(OutputR2));
  // Probe on OutputR2
  Register_HW Register4 (.CLK(clk), .Reset(reset), .WE(WE4), .InputA(RDVAL), .Result(OutputR4));
  Register_HW Register6 (.CLK(clk), .Reset(reset), .WE(WE6), .InputA(RDVAL), .Result(OutputR6));
  // Probe on OutputR4
  // Probe on OutputR6

  // Other names for the same wires on the sheet: RegisterWritenEnable = RegWE
endmodule

module SignExtension (
  input  [5:0] InputA,
  output [15:0] Result
);


  assign Result = {{11{InputA[5]}}, InputA[4:0]};
endmodule

module ALU (
  input  [15:0] InputA,
  input  [15:0] InputB,
  input  [2:0] OpType,
  output [15:0] aluOutput,
  output CmpOutput
);

  wire and_2_out, beq, bgt, bgt_re1, not_1_out;
  wire [14:0] Sub;
  wire [15:0] Add, andand, left_shift, right_shift, xorXor;

  assign andand = InputA & InputB;  // AND_Gate and_1, 16 bits wide
  assign xorXor = InputA ^ InputB;  // XOR_Gate xor_1, 16 bits wide
  SixteenAdder sixteenadder_1 (.AddSub(1'b1), .InputA(InputA), .InputB(InputB), .Sum({bgt_re1, Sub}));
  SixteenAdder sixteenadder_2 (.AddSub(1'b0), .InputA(InputA), .InputB(InputB), .Sum(Add));
  Shifter_HW shifter_hw_1 (.Input_num(InputB[2:0]), .InputA(InputA), .Result(left_shift));
  Multiplexer #(.select(3), .enable("false")) multiplexer_1 (
    .in6(beq), .in7(bgt), .out(CmpOutput), .sel(OpType));  // open: in0, in1, in2, in3, in4, in5
  Shifter_HW shifter_hw_2 (
    .Input_num(InputB[2:0]),
    .InputA({InputA[0], InputA[1], InputA[2], InputA[3], InputA[4], InputA[5], InputA[6], InputA[7], InputA[8], InputA[9], InputA[10], InputA[11], InputA[12], InputA[13], InputA[14], InputA[15]}),
    .Result({right_shift[0], right_shift[1], right_shift[2], right_shift[3], right_shift[4], right_shift[5], right_shift[6], right_shift[7], right_shift[8], right_shift[9], right_shift[10], right_shift[11], right_shift[12], right_shift[13], right_shift[14], right_shift[15]}));
  not not_1 (not_1_out, bgt_re1);
  or or_1 (beq, Sub[0], Sub[1], Sub[2], Sub[3], Sub[4], Sub[5], Sub[6], Sub[7], Sub[8], Sub[9], Sub[10], Sub[11], Sub[12], Sub[13], Sub[14], bgt_re1);
  and and_2 (and_2_out, not_1_out, beq);
  Multiplexer #(.select(3), .width(16), .enable("false")) multiplexer_2 (
    .in0(Add), .in1({bgt_re1, Sub}), .in2(left_shift), .in3(right_shift), .in4(andand), .in5(xorXor),
    .out(aluOutput), .sel(OpType));  // open: in6, in7
  not not_2 (bgt, and_2_out);

  // Other names for the same wires on the sheet: A[15:0] = InputA; B[15:0] = InputB; bgt_re2 = beq;
  //   shift_num[2:0] = InputB[2:0]; Sub[15] = bgt_re1
endmodule
